// Logisim project 2By4Encoder.circ as structural Verilog: 2 circuits, main circuit main
module main (
  input  in_1,
  input  in_2,
  output L1,
  output L2,
  output L3,
  output L4
);

  wire not_1_out, not_2_out, not_3_out, not_4_out;

  not not_1 (not_1_out, in_2);
  not not_2 (not_2_out, in_1);
  not not_3 (not_3_out, in_1);
  not not_4 (not_4_out, in_2);
  and _00 (L1, not_1_out, not_2_out);
  and _01 (L2, not_3_out, in_2);
  and _10 (L3, in_1, not_4_out);
  and _11 (L4, in_2, in_1);
endmodule

module Priority_Encoder (
  input  L0,
  input  L1,
  input  L2,
  input  L3,
  output Y,
  output X,
  output VALIDATION_BIT
);

  wire and_1_out, not_1_out;

  not not_1 (not_1_out, L2);
  or or_1 (X, L2, L3);
  and and_1 (and_1_out, L1, not_1_out);
  or or_2 (Y, and_1_out, L3);
  or or_3 (VALIDATION_BIT, L0, L1, L2, L3);
endmodule
