// Logisim project Project 2 Derick Hansraj.circ as structural Verilog: 1 circuit, main circuit main
module main (
  input  A,
  input  B,
  input  C,
  input  D,
  input  E,
  input  F,
  input  D1,
  input  C1,
  input  B1,
  input  A1,
  input  D1_2,
  input  C1_2,
  input  B1_2,
  input  A1_2,
  input  D1_3,
  input  C1_3,
  input  B1_3,
  input  A1_3,
  output out_19,
  output out_20,
  output out_21,
  output out_22,
  output out_23
);

  wire and_1_out, and_2_out, and_3_out, and_4_out, and_5_out, and_6_out, and_7_out, and_8_out, and_9_out,
       and_12_out, and_13_out, and_14_out, and_16_out, and_17_out, and_18_out, and_19_out, not_1_out,
       not_2_out, not_3_out, or_1_out, or_2_out, or_3_out, or_4_out, or_5_out, or_6_out, xnor_1_out,
       xnor_2_out, xnor_3_out, xnor_4_out, xnor_5_out, xnor_6_out, xor_1_out, xor_2_out, xor_3_out,
       xor_4_out, xor_5_out, xor_6_out, xor_8_out, xor_9_out;

  and and_1 (and_1_out, C1, A1);
  and and_2 (and_2_out, C1, B1);
  xor xor_1 (xor_1_out, A1, B1);
  and and_3 (and_3_out, C1_2, A1_2);
  and and_4 (and_4_out, C1_2, B1_2);
  and and_5 (and_5_out, B1, A1);
  and and_6 (and_6_out, C1_3, A1_3);
  and and_7 (and_7_out, C1_3, B1_3);
  not not_1 (not_1_out, D1);
  or or_1 (or_1_out, and_1_out, and_2_out);
  or or_2 (or_2_out, or_1_out, and_5_out);
  xor xor_2 (xor_2_out, xor_1_out, C1);
  and and_8 (and_8_out, B1_2, A1_2);
  xor xor_3 (xor_3_out, A1_2, B1_2);
  xnor xnor_1 (xnor_1_out, A, D);
  xnor xnor_2 (xnor_2_out, B, E);
  xnor xnor_3 (xnor_3_out, C, F);
  not not_2 (not_2_out, D1_2);
  and and_9 (and_9_out, B1_3, A1_3);
  xor xor_4 (xor_4_out, A1_3, B1_3);
  and and_10 (out_21, not_1_out, or_2_out);
  or or_3 (or_3_out, and_3_out, and_4_out);
  or or_4 (or_4_out, or_3_out, and_8_out);
  xor xor_5 (xor_5_out, xor_3_out, C1_2);
  not not_3 (not_3_out, D1_3);
  or or_5 (or_5_out, and_6_out, and_7_out);
  or or_6 (or_6_out, or_5_out, and_9_out);
  xor xor_6 (xor_6_out, xor_4_out, C1_3);
  and and_11 (out_19, xnor_1_out, xnor_2_out, xnor_2_out, xnor_3_out);
  and and_12 (and_12_out, and_5_out, C1);
  and and_13 (and_13_out, not_2_out, or_4_out);
  and and_14 (and_14_out, not_3_out, or_6_out);
  xor xor_7 (out_22, D1, xor_2_out);
  and and_15 (out_20, D1, and_12_out);
  and and_16 (and_16_out, and_8_out, C1_2);
  and and_17 (and_17_out, and_9_out, C1_3);
  xor xor_8 (xor_8_out, D1_2, xor_5_out);
  and and_18 (and_18_out, D1_2, and_16_out);
  xor xor_9 (xor_9_out, D1_3, xor_6_out);
  and and_19 (and_19_out, D1_3, and_17_out);
  xnor xnor_4 (xnor_4_out, and_18_out, and_19_out);
  xnor xnor_5 (xnor_5_out, and_13_out, and_14_out);
  xnor xnor_6 (xnor_6_out, xor_8_out, xor_9_out);
  and and_20 (out_23, xnor_4_out, xnor_5_out, xnor_5_out, xnor_6_out);

  // Notes on the sheet:
  //   Question 1
  //   Question 3
  //   Question 2
  //   Question 4
endmodule
