// Logisim project question3.circ as structural Verilog: 1 circuit, main circuit main
module main (
  input  A,
  input  B,
  input  C,
  output out_4
);

  wire and_1_out, and_2_out, not_1_out, not_3_out;

  not not_1 (not_1_out, A);
  // NOT_Gate not_2 has open pins: in=B, out=open
  not not_3 (not_3_out, C);
  and and_1 (and_1_out, not_1_out, C);
  and and_2 (and_2_out, B, A, not_3_out);
  or or_1 (out_4, and_1_out, and_2_out);
endmodule
