// Logisim project simple.circ as structural Verilog: 1 circuit, main circuit main
module main (
  input  in_1,
  input  in_2,
  input  in_3,
  output out_4,
  output out_5,
  output out_6,
  output out_7,
  output out_8
);

  not not_1 (out_5, in_2);
  and and_1 (out_6, in_2, in_3);
  or or_1 (out_8, in_3, in_1);
  xor xor_1 (out_7, out_6, out_8);

  assign out_4 = in_1;
endmodule
